// Logisim project cpu.circ as structural Verilog: 1 circuit, main circuit cpu
module cpu (
  input  clk,
  input  [31:0] Instruction,
  input  [31:0] MemReadData,
  output [31:0] MemAddress,
  output [31:0] ProgramCounter,
  output [31:0] ra,
  output [31:0] sp,
  output [31:0] t0,
  output [31:0] t1,
  output [31:0] t2,
  output [31:0] s0,
  output [31:0] s1,
  output [31:0] a0,
  output [3:0] MemWriteMask,
  output [31:0] MemWriteData
);

  wire ASel, BrEq, BrLt, BrUn, BSel, comparator_1_eq, comparator_2_eq, comparator_3_eq, comparator_4_eq,
       comparator_5_eq, comparator_6_eq, comparator_11_eq, comparator_12_eq, comparator_13_eq,
       comparator_14_eq, comparator_15_eq, comparator_16_eq, comparator_17_eq, comparator_18_eq,
       comparator_19_eq, comparator_20_eq, comparator_21_eq, comparator_22_gt, comparator_23_eq,
       comparator_24_eq, comparator_25_gt, comparator_26_eq, comparator_27_eq, comparator_28_gt,
       comparator_29_eq, Forward_rs2, is_ALUForwardA, is_ALUForwardB, is_imm, is_MemForwardA, is_MemForwardB,
       is_PC, is_ReadData1, is_ReadData2, LoadStall_Control, multiplexer_10_out, not_1_out, not_2_out,
       not_3_out, not_4_out, not_5_out, or_1_out, or_2_out, or_3_out, PCSel_EX, PCSel_IF, WBForward_rs1,
       WBForward_rs2;
  wire [1:0] ForwardA_Control, ForwardB_Control;
  wire [2:0] funct3;
  wire [3:0] ALUSel;
  wire [6:0] funct7;
  wire [14:0] Control, Control_EX, Control_MEM, Control_WB, multiplexer_9_out;
  wire [24:0] Instruction_ID;
  wire [31:0] ALUResult, ALUResult_EX, Immediate, Instruction_EX, Instruction_IF, Instruction_MEM,
       Instruction_WB, LoadData, multiplexer_2_out, multiplexer_5_out, multiplexer_6_out, multiplexer_7_out,
       multiplexer_8_out, multiplexer_11_out, multiplexer_13_out, NextPC, NextPC_EX, NextPC_ID, NextPC_MEM,
       PC_EX, PC_ID, ReadData1, ReadData1_EX, ReadData2, ReadData2_EX, Select_NextPC, SelectInstruction,
       WriteBack, WriteBack_ID, WriteData_EX, WriteData_MEM;

  Adder #(.width(32)) adder_1 (.a(ProgramCounter), .b(32'h4), .out(NextPC));  // open: cin, cout
  Multiplexer #(.width(32)) multiplexer_1 (.in0(Instruction), .in1(32'h13), .out(SelectInstruction), .sel(Control[0]));
  Multiplexer #(.width(32)) multiplexer_2 (
    .in0(Select_NextPC), .in1(ALUResult_EX), .out(multiplexer_2_out), .sel(PCSel_IF));
  Multiplexer #(.width(32)) multiplexer_3 (
    .in0(NextPC), .in1(ProgramCounter), .out(Select_NextPC), .sel(LoadStall_Control));
  Register #(.width(32)) PC (.D(multiplexer_2_out), .clk(clk), .Q(ProgramCounter));  // open: en, clr
  not not_1 (not_1_out, comparator_1_eq);
  Comparator #(.mode("unsigned"), .width(5)) comparator_1 (
    .a(Instruction_WB[11:7]), .b({5{1'b0}}), .eq(comparator_1_eq));  // open: gt, lt
  Comparator #(.mode("unsigned"), .width(5)) comparator_2 (
    .a(Instruction_WB[11:7]), .b(Instruction_EX[19:15]), .eq(comparator_2_eq));  // open: gt, lt
  Comparator #(.mode("unsigned"), .width(7)) comparator_3 (
    .a(Instruction_MEM[6:0]), .b(7'b0110011), .eq(comparator_3_eq));  // open: gt, lt
  Comparator #(.mode("unsigned"), .width(7)) comparator_4 (
    .a(Instruction_MEM[6:0]), .b(7'b0010011), .eq(comparator_4_eq));  // open: gt, lt
  Comparator #(.mode("unsigned"), .width(5)) comparator_5 (
    .a(Instruction_MEM[11:7]), .b({5{1'b0}}), .eq(comparator_5_eq));  // open: gt, lt
  Comparator #(.mode("unsigned"), .width(5)) comparator_6 (
    .a(Instruction_MEM[11:7]), .b(Instruction_EX[19:15]), .eq(comparator_6_eq));  // open: gt, lt
  Comparator #(.mode("unsigned"), .width(1)) comparator_7 (
    .a(Control_EX[6]), .b(1'b0), .eq(is_ReadData1));  // open: gt, lt
  Comparator #(.mode("unsigned"), .width(1)) comparator_8 (.a(Control_EX[6]), .b(1'b1), .eq(is_PC));  // open: gt, lt
  and and_1 (is_MemForwardA, Control_WB[1], not_1_out, comparator_2_eq);
  or or_1 (or_1_out, comparator_3_eq, comparator_4_eq);
  not not_2 (not_2_out, comparator_5_eq);
  and and_2 (is_ALUForwardA, or_1_out, not_2_out, comparator_6_eq);
  Multiplexer #(.width(32)) multiplexer_4 (
    .in0(SelectInstruction), .in1({funct7, Instruction_ID[24:15], funct3, Instruction_ID[11:0]}),
    .out(Instruction_IF), .sel(LoadStall_Control));
  Register #(.width(32)) register_1 (.D(Select_NextPC), .clk(clk), .Q(NextPC_ID));  // open: en, clr
  Register #(.width(32)) register_2 (.D(multiplexer_5_out), .clk(clk), .Q(PC_ID));  // open: en, clr
  Multiplexer #(.width(32)) multiplexer_5 (
    .in0(ProgramCounter), .in1(PC_ID), .out(multiplexer_5_out), .sel(LoadStall_Control));
  Register #(.width(32)) register_3 (
    .D(Instruction_IF), .clk(clk), .Q({funct7, Instruction_ID[24:15], funct3, Instruction_ID[11:0]}));  // open: en, clr
  control_logic control_logic_1 (
    .Instruction({funct7, Instruction_ID[24:15], funct3, Instruction_ID[11:0]}), .BrEq(BrEq), .BrLt(BrLt),
    .PCSel(Control[0]), .RegWEn(Control[1]), .ImmSel(Control[4:2]), .BrUn(BrUn), .ASel(ASel), .BSel(BSel),
    .ALUSel(ALUSel), .MemRW(Control[12]), .WBSel(Control[14:13]));
  Priority_Encoder #(.select_enc(2)) priority_encoder_1 (
    .in0(is_ReadData1), .in1(is_PC), .in2(is_MemForwardA), .in3(is_ALUForwardA), .out(ForwardA_Control));  // open: gs, en_out, en_in
  Comparator #(.mode("unsigned"), .width(1)) comparator_9 (
    .a(Control_EX[7]), .b(1'b0), .eq(is_ReadData2));  // open: gt, lt
  Comparator #(.mode("unsigned"), .width(1)) comparator_10 (.a(Control_EX[7]), .b(1'b1), .eq(is_imm));  // open: gt, lt
  not not_3 (not_3_out, comparator_11_eq);
  Comparator #(.mode("unsigned"), .width(5)) comparator_11 (
    .a(Instruction_WB[11:7]), .b({5{1'b0}}), .eq(comparator_11_eq));  // open: gt, lt
  Comparator #(.mode("unsigned"), .width(5)) comparator_12 (
    .a(Instruction_WB[11:7]), .b(Instruction_EX[24:20]), .eq(comparator_12_eq));  // open: gt, lt
  Comparator #(.mode("unsigned"), .width(7)) comparator_13 (
    .a(Instruction_MEM[6:0]), .b(7'b0110011), .eq(comparator_13_eq));  // open: gt, lt
  Comparator #(.mode("unsigned"), .width(7)) comparator_14 (
    .a(Instruction_MEM[6:0]), .b(7'b0010011), .eq(comparator_14_eq));  // open: gt, lt
  Comparator #(.mode("unsigned"), .width(5)) comparator_15 (
    .a(Instruction_MEM[11:7]), .b({5{1'b0}}), .eq(comparator_15_eq));  // open: gt, lt
  Comparator #(.mode("unsigned"), .width(5)) comparator_16 (
    .a(Instruction_MEM[11:7]), .b(Instruction_EX[24:20]), .eq(comparator_16_eq));  // open: gt, lt
  regfile regfile_1 (
    .ReadIndex1(Instruction_ID[19:15]), .ReadIndex2(Instruction_ID[24:20]),
    .WriteIndex(Instruction_WB[11:7]), .WriteData(WriteBack_ID), .RegWEn(Control_WB[1]), .clk(clk), .ra(ra),
    .sp(sp), .t0(t0), .t1(t1), .t2(t2), .s0(s0), .s1(s1), .a0(a0), .ReadData1(ReadData1),
    .ReadData2(ReadData2));
  and and_3 (is_MemForwardB, Control_WB[1], not_3_out, comparator_12_eq);
  or or_2 (or_2_out, comparator_13_eq, comparator_14_eq);
  not not_4 (not_4_out, comparator_15_eq);
  and and_4 (is_ALUForwardB, or_2_out, not_4_out, comparator_16_eq);
  Multiplexer #(.width(32)) multiplexer_6 (
    .in0(ReadData1), .in1(WriteBack_ID), .out(multiplexer_6_out), .sel(WBForward_rs1));
  Multiplexer #(.width(32)) multiplexer_7 (
    .in0(ReadData2), .in1(WriteBack_ID), .out(multiplexer_7_out), .sel(WBForward_rs2));
  Multiplexer #(.width(32)) multiplexer_8 (
    .in0({funct7, Instruction_ID[24:15], funct3, Instruction_ID[11:0]}), .in1(32'h13),
    .out(multiplexer_8_out), .sel(LoadStall_Control));
  Multiplexer #(.width(15)) multiplexer_9 (
    .in0({Control[14:12], ALUSel, BSel, ASel, BrUn, Control[4:0]}), .in1({15{1'b0}}),
    .out(multiplexer_9_out), .sel(LoadStall_Control));
  Multiplexer multiplexer_10 (.in0(Control[0]), .in1(1'b0), .out(multiplexer_10_out), .sel(LoadStall_Control));
  Register #(.width(32)) register_4 (.D(NextPC_ID), .clk(clk), .Q(NextPC_EX));  // open: en, clr
  Register #(.width(32)) register_5 (.D(PC_ID), .clk(clk), .Q(PC_EX));  // open: en, clr
  Register #(.width(32)) register_6 (.D(multiplexer_6_out), .clk(clk), .Q(ReadData1_EX));  // open: en, clr
  Register #(.width(32)) register_7 (.D(multiplexer_7_out), .clk(clk), .Q(ReadData2_EX));  // open: en, clr
  Register #(.width(32)) register_8 (.D(multiplexer_8_out), .clk(clk), .Q(Instruction_EX));  // open: en, clr
  Register #(.width(15)) register_9 (.D(multiplexer_9_out), .clk(clk), .Q(Control_EX));  // open: en, clr
  Register #(.width(1)) register_10 (.D(multiplexer_10_out), .clk(clk), .Q(PCSel_EX));  // open: en, clr
  Priority_Encoder #(.select_enc(2)) priority_encoder_2 (
    .in0(is_ReadData2), .in1(is_imm), .in2(is_MemForwardB), .in3(is_ALUForwardB), .out(ForwardB_Control));  // open: gs, en_out, en_in
  Multiplexer #(.select(2), .width(32)) multiplexer_11 (
    .in0(ReadData2_EX), .in1(Immediate), .in2(WriteBack_ID), .in3(MemAddress), .out(multiplexer_11_out),
    .sel(ForwardB_Control));
  Multiplexer #(.width(32)) multiplexer_12 (
    .in0(ReadData2_EX), .in1(MemAddress), .out(WriteData_EX), .sel(Forward_rs2));
  Comparator #(.mode("unsigned"), .width(5)) comparator_17 (
    .a(Instruction_EX[11:7]), .b({5{1'b0}}), .eq(comparator_17_eq));  // open: gt, lt
  Comparator #(.mode("unsigned"), .width(5)) comparator_18 (
    .a(Instruction_EX[11:7]), .b(Instruction_ID[19:15]), .eq(comparator_18_eq));  // open: gt, lt
  Comparator #(.mode("unsigned"), .width(5)) comparator_19 (
    .a(Instruction_EX[11:7]), .b(Instruction_ID[24:20]), .eq(comparator_19_eq));  // open: gt, lt
  Multiplexer #(.select(2), .width(32)) multiplexer_13 (
    .in0(ReadData1_EX), .in1(PC_EX), .in2(WriteBack_ID), .in3(MemAddress), .out(multiplexer_13_out),
    .sel(ForwardA_Control));
  Comparator #(.mode("unsigned"), .width(7)) comparator_20 (
    .a(Instruction_EX[6:0]), .b(7'b0000011), .eq(comparator_20_eq));  // open: gt, lt
  not not_5 (not_5_out, comparator_17_eq);
  or or_3 (or_3_out, comparator_18_eq, comparator_19_eq);
  alu alu_1 (.A(multiplexer_13_out), .B(multiplexer_11_out), .ALUSel(Control_EX[11:8]), .ALUResult(ALUResult));
  imm_gen imm_gen_1 (.Instruction(Instruction_EX), .ImmSel(Control_EX[4:2]), .Immediate(Immediate));
  branch_comp branch_comp_1 (
    .BrData1(ReadData1_EX), .BrData2(ReadData2_EX), .BrUn(Control_EX[5]), .BrEq(BrEq), .BrLt(BrLt));
  and and_5 (LoadStall_Control, comparator_20_eq, not_5_out, or_3_out);
  Register #(.width(32)) register_11 (.D(NextPC_EX), .clk(clk), .Q(NextPC_MEM));  // open: en, clr
  Register #(.width(32)) register_12 (.D(ALUResult), .clk(clk), .Q(MemAddress));  // open: en, clr
  Register #(.width(32)) register_13 (.D(WriteData_EX), .clk(clk), .Q(WriteData_MEM));  // open: en, clr
  Register #(.width(32)) register_14 (.D(Instruction_EX), .clk(clk), .Q(Instruction_MEM));  // open: en, clr
  Register #(.width(15)) register_15 (.D(Control_EX), .clk(clk), .Q(Control_MEM));  // open: en, clr
  Register #(.width(1)) register_16 (.D(PCSel_EX), .clk(clk), .Q(PCSel_IF));  // open: en, clr
  Comparator #(.mode("unsigned"), .width(1)) comparator_21 (
    .a(Control_WB[1]), .b(1'b1), .eq(comparator_21_eq));  // open: gt, lt
  Comparator #(.mode("unsigned"), .width(5)) comparator_22 (
    .a(Instruction_WB[11:7]), .b({5{1'b0}}), .gt(comparator_22_gt));  // open: eq, lt
  Comparator #(.mode("unsigned"), .width(5)) comparator_23 (
    .a(Instruction_WB[11:7]), .b(Instruction_ID[19:15]), .eq(comparator_23_eq));  // open: gt, lt
  Comparator #(.mode("unsigned"), .width(1)) comparator_24 (
    .a(Control_WB[1]), .b(1'b1), .eq(comparator_24_eq));  // open: gt, lt
  Comparator #(.mode("unsigned"), .width(5)) comparator_25 (
    .a(Instruction_WB[11:7]), .b({5{1'b0}}), .gt(comparator_25_gt));  // open: eq, lt
  Comparator #(.mode("unsigned"), .width(5)) comparator_26 (
    .a(Instruction_WB[11:7]), .b(Instruction_ID[24:20]), .eq(comparator_26_eq));  // open: gt, lt
  and and_6 (WBForward_rs1, comparator_21_eq, comparator_22_gt, comparator_23_eq);
  and and_7 (WBForward_rs2, comparator_24_eq, comparator_25_gt, comparator_26_eq);
  partial_store partial_store_1 (
    .Instruction(Instruction_MEM), .MemAddress(MemAddress), .DataFromReg(WriteData_MEM),
    .MemRW(Control_MEM[12]), .MemWriteMask(MemWriteMask), .DataToMem(MemWriteData));
  partial_load partial_load_1 (
    .Instruction(Instruction_MEM), .MemAddress(MemAddress), .DataFromMem(MemReadData), .DataToReg(LoadData));
  Multiplexer #(.select(2), .width(32)) multiplexer_14 (
    .in0(LoadData), .in1(MemAddress), .in2(NextPC_MEM), .out(WriteBack), .sel(Control_MEM[14:13]));  // open: in3
  Comparator #(.mode("unsigned"), .width(1)) comparator_27 (
    .a(Control_MEM[1]), .b(1'b1), .eq(comparator_27_eq));  // open: gt, lt
  Comparator #(.mode("unsigned"), .width(5)) comparator_28 (
    .a(Instruction_MEM[11:7]), .b({5{1'b0}}), .gt(comparator_28_gt));  // open: eq, lt
  Comparator #(.mode("unsigned"), .width(5)) comparator_29 (
    .a(Instruction_MEM[11:7]), .b(Instruction_EX[24:20]), .eq(comparator_29_eq));  // open: gt, lt
  and and_8 (Forward_rs2, comparator_27_eq, comparator_28_gt, comparator_29_eq);
  Register #(.width(32)) register_17 (.D(WriteBack), .clk(clk), .Q(WriteBack_ID));  // open: en, clr
  Register #(.width(32)) register_18 (.D(Instruction_MEM), .clk(clk), .Q(Instruction_WB));  // open: en, clr
  Register #(.width(15)) register_19 (.D(Control_MEM), .clk(clk), .Q(Control_WB));  // open: en, clr

  // Other names for the same wires on the sheet: ALUResult_MEM[31:0] = MemAddress; PCSel = Control[0];
  //   RegWEn = Control[1]; ImmSel[2:0] = Control[4:2]; Control[11:5] = {ALUSel, BSel, ASel, BrUn};
  //   MemRW = Control[12]; WBSel[1:0] = Control[14:13]; opcode[6:0] = Instruction_ID[6:0];
  //   rd[4:0] = Instruction_ID[11:7]; Instruction_ID (some bits) = {funct7, funct3}; rs1[4:0] = Instruction_ID[19:15];
  //   rs2[4:0] = Instruction_ID[24:20]

  // Notes on the sheet:
  //   Additional Control Logic for Forwarding
  //   To IMEM
  //   IMEM (do **NOT** move this)
  //   From IMEM
  //   Control Logic Pipelining
  //   Inputs/Outputs for testing. Do **NOT** move these.
  //   It is OK to move the PC, RegFile, ALU, MEM, Branch Comp, Imm Gen, Partial Load, Partial Store and Control Logic to wherever is most convenient for you when constructing your CPU, and to delete this text
  //   To DMEM
  //   DMEM (do **NOT** move this)
  //   From DMEM
  //   Additional Control Logic for Stall
  //   Additional Data Forwarding for WB data
  //   Regfile cannot load the written data in the same cycle
  //   Additional Data Forwarding for Store Data (rs2)
endmodule
